# Fritzing sketch Display on Arduino of System Information Bar with Micropython - fritzing (saved by Fritzing 0.9.3b)

parts:
  U1 = NodeMCU V3.0
  Componente1 = LCD1602-I2C

nets:
  N1: U1.D1, Componente1.SCL
  N2: U1.D2, Componente1.SDA
  GND: U1.GND, Componente1.GND
  VIN: U1.Vin, Componente1.VCC

custom parts:
  NodeMCU V3.0: ESP8266 based NodeMCU
  LCD1602-I2C: A standard character display, usually with 2x16 characters. Comes in many colors with LCM1602 IIC attached.
